# Fritzing sketch Board1 (saved by Fritzing 0.9.3b)
breadboards: 1

parts:
  Part1 = Adafruit Ultimate GPS v3 [part_number="Adafruit #746"]
  JP1 = Header 10 [package=1x10-2mm-smd]
  Part2 = Adafruit T-Cobbler Plus [part_number="Adafruit #1989 and #2028"]  # not connected
  Raspberry_Pi_1 = Raspberry Pi 3 [part_number=RPI-3-V1.2]  # not connected

nets:
  N1: Part1.RX, JP1.4
  N2: Part1.TX, JP1.5
  N3: Part1.FIX, JP1.6

custom parts:
  Adafruit Ultimate GPS v3: We carry a few different GPS modules here in the Adafruit shop, but none that satisfied our every desire - that's why we designed this little GPS breakout board. We believe this is the Ultimate GPS module, so we named it that. It's got everything you want and more: -165 dBm sensitivity, 10 Hz updates, 66 channels 5V friendly design and only 20mA current draw Breadboard friendly + two mounting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
  Adafruit T-Cobbler Plus: The Raspberry Pi has landed on the Maker World like a 40-GPIO pinned, quad-USB ported, credit card sized bomb of DIY joy. And while you can use most of our great Model B accessories by hooking up our downgrade cable, its probably a good time to upgrade your set up and accessorize using all of the 40 pins. That's why we now carry the Assembled Adafruit Pi T-Cobbler Plus - Breakout + Cable for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
